# Fritzing sketch f1 (saved by Fritzing 0.9.4)
breadboards: 1

parts:
  Part1 = Arduino Uno (Rev3)
  LED1 = LED - 5mm [color="Red (633nm)" package="5 mm [THT]"]
  LED2 = LED - 5mm [color="Red (633nm)" package="5 mm [THT]"]
  LED3 = LED - 5mm [color="Red (633nm)" package="5 mm [THT]"]
  LED4 = LED - 5mm [color="Red (633nm)" package="5 mm [THT]"]
  R1 = Resistor [tolerance=±5% resistance=330 package=THT]
  R2 = Resistor [tolerance=±5% resistance=330 package=THT]
  R3 = Resistor [tolerance=±5% resistance=330 package=THT]
  R4 = Resistor [tolerance=±5% resistance=330 package=THT]
  R5 = Resistor [tolerance=±5% resistance=330 package=THT]
  S1 = Pushbutton [package="[THT]"]
  S2 = Pushbutton [package="[THT]"]
  LCD1 = LCD screen
  R7 = Resistor [tolerance=±5% resistance=220 package=THT]
  R8 = Resistor [tolerance=±5% resistance=220 package=THT]
  R9 = Resistor [tolerance=±5% resistance=220 package=THT]
  Buzzer = Piezo Speaker
  R10 = Resistor [tolerance=±5% resistance=10k package=THT]
  R11 = Resistor [tolerance=±5% resistance=10k package=THT]
  LED5 = LED - 5mm [color="Red (633nm)" package="5 mm [THT]"]
  S3 = Reed switch [package=THT]
  S4 = Reed switch [package=THT]

nets:
  N1: Part1.A1, R8.Pin_1, S3.pin_1
  N2: Part1.A2, R9.Pin_1, S4.pin_1
  N3: Part1.A3, S1.Pin_1, S1.Pin_2, R11.Pin_0
  N4: Part1.A4/SDA, S2.Pin_1, S2.Pin_2, R10.Pin_0
  N5: Part1.D8, LCD1.E
  N6: Part1.D9_PWM, LED5.anode
  N7: Part1.D10_PWM/SS, LED4.anode
  N8: Part1.D11_PWM/MOSI, LED3.anode
  N9: Part1.D12/MISO, LED2.anode
  N10: Part1.D13/SCK, LED1.anode
  GND: Part1.GND, R1.Pin_1, R2.Pin_1, R3.Pin_1, R4.Pin_1, R5.Pin_1, LCD1.VSS, LCD1.R/W, LCD1.LED-, Buzzer.pin1, R10.Pin_1, R11.Pin_1, S3.pin_2, S4.pin_2
  N11: Part1.D2, Buzzer.pin2
  N12: Part1.D3_PWM, LCD1.RS
  N13: Part1.D4, LCD1.DB7
  N14: Part1.D5_PWM, LCD1.DB6
  N15: Part1.D6_PWM, LCD1.DB5
  N16: Part1.D7, LCD1.DB4
  5V: Part1.5V, S1.Pin_3, S1.Pin_4, S2.Pin_3, S2.Pin_4, LCD1.VDD, R7.Pin_0, R8.Pin_0, R9.Pin_0
  N17: LED1.cathode, R1.Pin_0
  N18: LED2.cathode, R2.Pin_0
  N19: LED3.cathode, R3.Pin_0
  N20: LED4.cathode, R4.Pin_0
  N21: R5.Pin_0, LED5.cathode
  N22: LCD1.LED+, R7.Pin_1
